// Logisim project additioneur.circ as structural Verilog: 1 circuit, main circuit main
module main (
  input  _1,
  input  in_2,
  input  _2,
  input  in_4,
  input  _3,
  input  in_6,
  output out_7,
  output out_8,
  output out_9,
  output out_10
);

  wire and_1_out, and_2_out, and_3_out, and_4_out, and_5_out, or_1_out, xor_2_out, xor_3_out;

  xor xor_1 (out_7, _1, in_2);
  and and_1 (and_1_out, _1, in_2);
  xor xor_2 (xor_2_out, and_1_out, _2);
  and and_2 (and_2_out, and_1_out, _2);
  xor xor_3 (xor_3_out, or_1_out, _3);
  and and_3 (and_3_out, or_1_out, _3);
  and and_4 (and_4_out, xor_2_out, in_4);
  xor xor_4 (out_8, xor_2_out, in_4);
  or or_1 (or_1_out, and_4_out, and_2_out);
  xor xor_5 (out_9, xor_3_out, in_6);
  and and_5 (and_5_out, xor_3_out, in_6);
  or or_2 (out_10, and_5_out, and_3_out);
endmodule
