// Logisim project gate.circ as structural Verilog: 1 circuit, main circuit main
module main (
  input  in_1,
  input  in_2,
  input  in_3,
  input  in_4,
  input  in_5,
  input  in_6,
  input  in_7,
  input  in_8,
  input  in_9,
  input  in_10,
  input  in_11,
  input  in_12,
  input  in_13,
  input  in_14,
  output out_15,
  output out_16,
  output out_17,
  output out_18,
  output out_19,
  output out_20
);

  wire and_1_out, and_2_out, nand_1_out, nand_2_out, nand_3_out, nand_4_out, nand_7_out, nand_8_out,
       nand_9_out, nor_1_out, nor_2_out, nor_3_out;

  nand nand_1 (nand_1_out, in_1, in_1);
  nand nand_2 (nand_2_out, in_3, in_4);
  nand nand_3 (nand_3_out, in_6, in_6);
  nand nand_4 (nand_4_out, in_7, in_7);
  nor nor_1 (nor_1_out, in_8, in_8);
  nor nor_2 (nor_2_out, in_9, in_9);
  nor nor_3 (nor_3_out, in_10, in_11);
  and and_1 (and_1_out, in_12, in_13);
  and and_2 (and_2_out, in_14, in_14);
  nand nand_5 (out_15, nand_2_out, nand_2_out);
  nand nand_6 (out_17, nand_3_out, nand_4_out);
  nor nor_4 (out_18, nor_1_out, nor_2_out);
  not nor_5 (out_19, nor_3_out);  // NOR_Gate
  and and_3 (out_20, and_1_out, and_2_out);
  LED led_1 (.in(nand_1_out));
  nand nand_7 (nand_7_out, in_2, in_5);
  nand nand_8 (nand_8_out, in_2, nand_7_out);
  nand nand_9 (nand_9_out, nand_7_out, in_5);
  nand nand_10 (out_16, nand_8_out, nand_9_out);
endmodule
