// Logisim project test_controle_multiplexeur.circ as structural Verilog: 1 circuit, main circuit main
module main (
  input  in_1,
  input  in_2,
  input  in_3,
  input  in_4,
  input  in_5,
  output out_6,
  output out_7,
  output out_8,
  output out_9
);

  wire not_1_out, not_2_out, not_3_out, not_4_out;

  Multiplexer multiplexer_1 (.in0(in_1), .in1(not_1_out), .out(out_6), .sel(in_5));  // open: en
  not not_1 (not_1_out, in_1);
  Multiplexer multiplexer_2 (.in0(in_2), .in1(not_2_out), .out(out_7), .sel(in_5));  // open: en
  not not_2 (not_2_out, in_2);
  Multiplexer multiplexer_3 (.in0(in_3), .in1(not_3_out), .out(out_8), .sel(in_5));  // open: en
  not not_3 (not_3_out, in_3);
  Multiplexer multiplexer_4 (.in0(in_4), .in1(not_4_out), .out(out_9), .sel(in_5));  // open: en
  not not_4 (not_4_out, in_4);
endmodule
